# Fritzing sketch DDIS_ProtoShieldArduino (saved by Fritzing 0.9.2b)
circuit board: 10cm x 6.5cm

parts:
  SPC5_DDIS_Arduino_Shield = SPC56 D Discovery [package=THT]

nets:
  N1: SPC5_DDIS_Arduino_Shield.PB[2], SPC5_DDIS_Arduino_Shield.RX
  N2: SPC5_DDIS_Arduino_Shield.GND#2, SPC5_DDIS_Arduino_Shield.GND#80
  N3: SPC5_DDIS_Arduino_Shield.PA[0], SPC5_DDIS_Arduino_Shield.D2
  N4: SPC5_DDIS_Arduino_Shield.PB[9], SPC5_DDIS_Arduino_Shield.A5
  N5: SPC5_DDIS_Arduino_Shield.PB[3], SPC5_DDIS_Arduino_Shield.TX
  N6: SPC5_DDIS_Arduino_Shield.GND#20, SPC5_DDIS_Arduino_Shield.GND#81
  N7: SPC5_DDIS_Arduino_Shield.PA[2], SPC5_DDIS_Arduino_Shield.D4
  N8: SPC5_DDIS_Arduino_Shield.PA[1], SPC5_DDIS_Arduino_Shield.D3
  N9: SPC5_DDIS_Arduino_Shield.PA[4], SPC5_DDIS_Arduino_Shield.D6
  N10: SPC5_DDIS_Arduino_Shield.PB[8], SPC5_DDIS_Arduino_Shield.A4
  N11: SPC5_DDIS_Arduino_Shield.PA[6], SPC5_DDIS_Arduino_Shield.D8
  N12: SPC5_DDIS_Arduino_Shield.GND#34, SPC5_DDIS_Arduino_Shield.GND#73
  N13: SPC5_DDIS_Arduino_Shield.PA[10], SPC5_DDIS_Arduino_Shield.D12
  N14: SPC5_DDIS_Arduino_Shield.PA[8], SPC5_DDIS_Arduino_Shield.D10
  N15: SPC5_DDIS_Arduino_Shield.PB[7], SPC5_DDIS_Arduino_Shield.A3
  N16: SPC5_DDIS_Arduino_Shield.PB[5], SPC5_DDIS_Arduino_Shield.A1
  N17: SPC5_DDIS_Arduino_Shield.PA[5], SPC5_DDIS_Arduino_Shield.D7
  N18: SPC5_DDIS_Arduino_Shield.PA[11], SPC5_DDIS_Arduino_Shield.D13
  N19: SPC5_DDIS_Arduino_Shield.PA[9], SPC5_DDIS_Arduino_Shield.D11
  N20: SPC5_DDIS_Arduino_Shield.PA[7], SPC5_DDIS_Arduino_Shield.D9
  N21: SPC5_DDIS_Arduino_Shield.PA[3], SPC5_DDIS_Arduino_Shield.D5
  N22: SPC5_DDIS_Arduino_Shield.PB[6], SPC5_DDIS_Arduino_Shield.A2
  N23: SPC5_DDIS_Arduino_Shield.PB[4], SPC5_DDIS_Arduino_Shield.A0

custom parts:
  SPC56 D Discovery: The SPC560D-DIS discovery board is an evaluation tool supporting STMicroelectronics SPC56 D line microcontrollers. The evaluation board allows full access to all CPUs I/O signals and to peripherals.
