# Fritzing sketch ProtoShieldArduino-03 (saved by Fritzing 0.9.2b)
circuit board: 10.826cm x 7.11415cm

parts:
  U1 = SPC56 D Discovery [package=THT]

nets:
  N1: U1.PB[2], U1.RX
  N2: U1.GND#2, U1.GND#80
  N3: U1.PA[0], U1.D2
  N4: U1.PB[9], U1.A5
  N5: U1.PB[3], U1.TX
  N6: U1.GND#20, U1.GND#81
  N7: U1.PA[2], U1.D4
  N8: U1.PA[1], U1.D3
  N9: U1.PA[4], U1.D6
  N10: U1.PB[8], U1.A4
  N11: U1.PA[6], U1.PC[2], U1.D8
  N12: U1.PA[10], U1.D13
  N13: U1.PA[8], U1.D11
  N14: U1.PB[7], U1.A3
  N15: U1.PB[5], U1.A1
  N16: U1.PA[5], U1.PC[3], U1.D7
  N17: U1.PA[11], U1.GND#73
  N18: U1.PA[9], U1.D12
  N19: U1.PA[7], U1.D9, U1.D10
  N20: U1.PA[3], U1.D5
  N21: U1.PB[6], U1.A2
  N22: U1.PB[4], U1.A0

custom parts:
  SPC56 D Discovery: The SPC560D-DIS discovery board is an evaluation tool supporting STMicroelectronics SPC56 D line microcontrollers. The evaluation board allows full access to all CPUs I/O signals and to peripherals.
