# Fritzing sketch ProtoShieldArduino (saved by Fritzing 0.9.2b)
circuit board: 9.74436cm x 6.85685cm
perfboards: 1

parts:
  J1 = female pin header, 36 pins [form="♀ (female)"]
  J2 = female pin header, 36 pins [form="♀ (female)"]
  J4 = female pin header, 36 pins [form="♀ (female)"]
  J3 = female pin header, 36 pins [form="♀ (female)"]
  J8 = female pin header, 8 pins [form="♀ (female)"]
  J7 = female pin header, 6 pins [form="♀ (female)"]
  J5 = female pin header, 8 pins [form="♀ (female)"]
  J6 = female pin header, 10 pins [form="♀ (female)"]
  J9 = female pin header, 15 pins [form="♀ (female)"]  # not connected
  J10 = female pin header, 15 pins [form="♀ (female)"]  # not connected
  J11 = female pin header, 10 pins [form="♀ (female)"]  # not connected

nets:
  N1: J1.pin10, J5.pin2
  N2: J1.pin19, J5.pin3
  N3: J1.pin20, J8.pin7
  N4: J1.pin22, J8.pin3
  N5: J1.pin32, J7.pin1
  N6: J2.pin10, J5.pin1
  N7: J2.pin15, J5.pin5
  N8: J2.pin16, J5.pin4
  N9: J2.pin22, J8.pin2
  N10: J2.pin30, J5.pin7
  N11: J2.pin32, J7.pin2
  N12: J2.pin36, J8.pin5
  N13: J4.pin5, J5.pin8
  N14: J4.pin10, J6.pin6
  N15: J4.pin12, J6.pin4
  N16: J4.pin13, J6.pin2
  N17: J4.pin19, J5.pin6
  N18: J4.pin27, J7.pin4
  N19: J4.pin28, J7.pin6
  N20: J3.pin5, J6.pin1
  N21: J3.pin11, J6.pin7
  N22: J3.pin12, J6.pin5
  N23: J3.pin13, J6.pin3
  N24: J3.pin27, J7.pin3
  N25: J3.pin28, J7.pin5
